# Fritzing sketch schema (saved by Fritzing 0.9.3b)
breadboards: 1

parts:
  WeMos_D1_R1 = WeMos D1 R2
  S1 = Pushbutton [package="[THT]"]
  S2 = Pushbutton [package="[THT]"]
  R1 = Resistor [tolerance=±5% resistance=220 package=THT]
  R2 = Resistor [tolerance=±5% resistance=1k package=THT]
  LED1 = RGB LED (com. cathode, rgb) [package="5 mm [THT]"]

nets:
  N1: WeMos_D1_R1.D2, WeMos_D1_R1.GND, R1.Pin_1, R2.Pin_1, LED1.green_anode, LED1.blue_anode
  N2: WeMos_D1_R1.D3, LED1.common_cathode
  N3: WeMos_D1_R1.D4, LED1.red_anode
  N4: WeMos_D1_R1.(D5), S1.Pin_3, S1.Pin_4, R2.Pin_0
  N5: WeMos_D1_R1.(D6), S2.Pin_3, S2.Pin_4, R1.Pin_0
  N6: WeMos_D1_R1.3.3V, S1.Pin_1, S1.Pin_2, S2.Pin_1, S2.Pin_2

custom parts:
  WeMos D1 R2: The D1 R2 is a mini wifi board based on the ESP-8266EX.
